// Logisim project Project 4 but its done though.circ as structural Verilog: 3 circuits, main circuit main
module main (
  input  [15:0] Operand_1__Multiplicand_or_Dividend,
  input  [15:0] Operand_2__Multiplier_and_Divisor,
  input  Mul,
  input  Div,
  output [31:0] Product,
  output M_Ready,
  output [15:0] Quotient,
  output [15:0] Remainder,
  output D_Ready
);

  wire Clock_out;
  wire [31:0] n16_bit_multiplication_1_product;

  _16_bit_Multiplication u_16_bit_multiplication_1 (
    .Multiplicand(Operand_1__Multiplicand_or_Dividend), .Multiplier(Operand_2__Multiplier_and_Divisor),
    .Mul(Mul), .Clock(Clock_out), .Product(n16_bit_multiplication_1_product), .M_Ready(M_Ready));
  // Probe on Clock_out
  Clock Clock (.out(Clock_out));
  // Probe on n16_bit_multiplication_1_product
  Multiplexer #(.width(32), .enable("false")) multiplexer_1 (
    .in0({32{1'b0}}), .in1(n16_bit_multiplication_1_product), .out(Product), .sel(M_Ready));
endmodule

module _16_bit_Multiplication (
  input  [15:0] Multiplicand,
  input  [15:0] Multiplier,
  input  Mul,
  input  Clock,
  output [31:0] Product,
  output M_Ready
);

  wire and_1_out, not_1_out, not_2_out;
  wire [7:0] counter_1_q, rom_1_data;
  wire [15:0] multiplexer_2_out, multiplier_q, shifter_2_out;
  wire [31:0] adder_1_out, multiplexer_1_out, multiplexer_3_out, multiplicand_q, shifter_1_out;

  Counter #(.max('h11), .ongoal("stay")) counter_1 (
    .Q(counter_1_q), .carry(M_Ready), .clk(and_1_out), .clr(not_1_out));  // open: load, D, count
  not not_1 (not_1_out, Mul);
  and and_1 (and_1_out, Mul, Clock);
  Multiplexer #(.width(32), .enable("false")) multiplexer_1 (
    .in0(shifter_1_out), .in1({{16{1'b0}}, Multiplicand}), .out(multiplexer_1_out), .sel(rom_1_data[0]));
  Multiplexer #(.width(16), .enable("false")) multiplexer_2 (
    .in0(shifter_2_out), .in1(Multiplier), .out(multiplexer_2_out), .sel(rom_1_data[0]));
  ROM rom_1 (.addr(counter_1_q), .data(rom_1_data));  // open: sel
  Register #(.width(32)) u_multiplicand (.D(multiplexer_1_out), .Q(multiplicand_q), .clk(and_1_out));  // open: en, clr
  Register #(.width(16)) u_multiplier (.D(multiplexer_2_out), .Q(multiplier_q), .clk(and_1_out));  // open: en, clr
  Shifter #(.width(32)) shifter_1 (.in(multiplicand_q), .\dist (5'b00001), .out(shifter_1_out));
  Multiplexer #(.width(32), .enable("false")) multiplexer_3 (
    .in0(multiplicand_q), .in1({32{1'b0}}), .out(multiplexer_3_out), .sel(not_2_out));
  Shifter #(.width(16), .shift("lr")) shifter_2 (.in(multiplier_q), .\dist (4'b0001), .out(shifter_2_out));
  not not_2 (not_2_out, multiplier_q[0]);
  Adder #(.width(32)) adder_1 (.a(Product), .b(multiplexer_3_out), .out(adder_1_out));  // open: cin, cout
  Register #(.width(32)) u_product (.D(adder_1_out), .Q(Product), .clk(and_1_out), .clr(rom_1_data[0]));  // open: en

  // Notes on the sheet:
  //   When the Two bit is 1, shift multiplicand
  //   When the Three bit is 1, shift multiplier
  //   When the Zero bit is 1, the product, multiplicand, and multiplier are initialized
  //   When the One bit is 1, perform product = product + multiplicand*multiplier0
  //   contents of rom_1 (hex, n*v repeats v):
  //   1
  //   Clock to Registers
endmodule

module _16_bit_Division (
  input  [15:0] Divisor,
  input  [15:0] Dividend,
  input  Div,
  input  Clock,
  output [15:0] Quotient,
  output [15:0] Remainder,
  output D_Ready
);

  wire and_1_out, not_1_out;
  wire [7:0] counter_1_q, rom_1_data;

  ROM rom_1 (.addr(counter_1_q), .data(rom_1_data));  // open: sel
  Counter #(.ongoal("stay")) counter_1 (
    .Q(counter_1_q), .carry(D_Ready), .clk(and_1_out), .clr(not_1_out));  // open: load, D, count
  not not_1 (not_1_out, Div);
  and and_1 (and_1_out, Div, Clock);

  // Notes on the sheet:
  //   Clock to Registers
endmodule
