// Logisim project Project 4 even worse.circ as structural Verilog: 4 circuits, main circuit main
module main (
  input  [15:0] Operand_1__Multiplicand_or_Dividend,
  input  [15:0] Operand_2__Multiplier_and_Divisor,
  input  Mul,
  input  Div,
  output [31:0] Product,
  output M_Ready,
  output [15:0] Quotient,
  output [15:0] Remainder,
  output D_Ready
);

  wire and_1_out, and_2_out, Clock_out, negative_tester_1_negated, negative_tester_2_negated, not_1_out,
       not_2_out, or_1_out;
  wire [15:0] negative_tester_1_absolute_value, negative_tester_2_absolute_value;
  wire [31:0] multiplexer_1_out, n16_bit_multiplication_1_product, negator_1_out;

  not not_1 (not_1_out, negative_tester_1_negated);
  not not_2 (not_2_out, negative_tester_2_negated);
  and and_1 (and_1_out, negative_tester_2_negated, not_1_out);
  and and_2 (and_2_out, not_2_out, negative_tester_1_negated);
  or or_1 (or_1_out, and_1_out, and_2_out);
  Negative_Tester negative_tester_1 (
    .Input(Operand_1__Multiplicand_or_Dividend), .Absolute_Value(negative_tester_1_absolute_value),
    .Negated(negative_tester_1_negated));
  Negative_Tester negative_tester_2 (
    .Input(Operand_2__Multiplier_and_Divisor), .Absolute_Value(negative_tester_2_absolute_value),
    .Negated(negative_tester_2_negated));
  _16_bit_Multiplication u_16_bit_multiplication_1 (
    .Multiplicand(negative_tester_1_absolute_value), .Multiplier(negative_tester_2_absolute_value),
    .Mul(Mul), .Clock(Clock_out), .Product(n16_bit_multiplication_1_product), .M_Ready(M_Ready));
  Clock Clock (.out(Clock_out));
  // Probe on n16_bit_multiplication_1_product
  Multiplexer #(.width(32), .enable("false")) multiplexer_1 (
    .in0({32{1'b0}}), .in1(n16_bit_multiplication_1_product), .out(multiplexer_1_out), .sel(M_Ready));
  Negator #(.width(32)) negator_1 (.in(multiplexer_1_out), .out(negator_1_out));
  Multiplexer #(.width(32), .enable("false")) multiplexer_2 (
    .in0(multiplexer_1_out), .in1(negator_1_out), .out(Product), .sel(or_1_out));
endmodule

module _16_bit_Multiplication (
  input  [15:0] Multiplicand,
  input  [15:0] Multiplier,
  input  Mul,
  input  Clock,
  output [31:0] Product,
  output M_Ready
);

  wire and_1_out, not_1_out, not_2_out;
  wire [7:0] counter_1_q, rom_1_data;
  wire [15:0] multiplexer_2_out, multiplier_q, shifter_2_out;
  wire [31:0] adder_1_out, multiplexer_1_out, multiplexer_3_out, multiplicand_q, shifter_1_out;

  Counter #(.max('h11), .ongoal("stay")) counter_1 (
    .Q(counter_1_q), .carry(M_Ready), .clk(and_1_out), .clr(not_1_out));  // open: load, D, count
  not not_1 (not_1_out, Mul);
  and and_1 (and_1_out, Mul, Clock);
  Multiplexer #(.width(32), .enable("false")) multiplexer_1 (
    .in0(shifter_1_out), .in1({{16{1'b0}}, Multiplicand}), .out(multiplexer_1_out), .sel(rom_1_data[0]));
  Multiplexer #(.width(16), .enable("false")) multiplexer_2 (
    .in0(shifter_2_out), .in1(Multiplier), .out(multiplexer_2_out), .sel(rom_1_data[0]));
  ROM rom_1 (.addr(counter_1_q), .data(rom_1_data));  // open: sel
  Register #(.width(32)) u_multiplicand (.D(multiplexer_1_out), .Q(multiplicand_q), .clk(and_1_out));  // open: en, clr
  Register #(.width(16)) u_multiplier (.D(multiplexer_2_out), .Q(multiplier_q), .clk(and_1_out));  // open: en, clr
  Shifter #(.width(32)) shifter_1 (.in(multiplicand_q), .\dist (5'b00001), .out(shifter_1_out));
  Multiplexer #(.width(32), .enable("false")) multiplexer_3 (
    .in0(multiplicand_q), .in1({32{1'b0}}), .out(multiplexer_3_out), .sel(not_2_out));
  not not_2 (not_2_out, multiplier_q[0]);
  Shifter #(.width(16), .shift("lr")) shifter_2 (.in(multiplier_q), .\dist (4'b0001), .out(shifter_2_out));
  Adder #(.width(32)) adder_1 (.a(Product), .b(multiplexer_3_out), .out(adder_1_out));  // open: cin, cout
  Register #(.width(32)) u_product (.D(adder_1_out), .Q(Product), .clk(and_1_out), .clr(rom_1_data[0]));  // open: en

  // Notes on the sheet:
  //   Multiplication requires 17 clock cycles to complete
  //   When the Zero bit is 1, the product, multiplicand, and multiplier are initialized
  //   contents of rom_1 (hex, n*v repeats v):
  //   1
  //   Clock to Registers
endmodule

module _16_bit_Division (
  input  [15:0] Divisor,
  input  [15:0] Dividend,
  input  Div,
  input  Clock,
  output [15:0] Quotient,
  output [15:0] Remainder,
  output D_Ready
);

  wire and_1_out, not_1_out;
  wire [7:0] counter_1_q, rom_1_data;
  wire [15:0] adder_1_out, multiplexer_4_out, Quotient_q;
  wire [31:0] Divisor_q, multiplexer_1_out, multiplexer_2_out, multiplexer_3_out, shifter_1_out;
  wire [31:16] Remainder_q;

  ROM rom_1 (.addr(counter_1_q), .data(rom_1_data));  // open: sel
  Counter #(.max('h11), .ongoal("stay")) counter_1 (
    .Q(counter_1_q), .carry(D_Ready), .clk(and_1_out), .clr(not_1_out));  // open: load, D, count
  not not_1 (not_1_out, Div);
  and and_1 (and_1_out, Div, Clock);
  Multiplexer #(.width(32), .enable("false")) multiplexer_1 (
    .in0(shifter_1_out), .in1({Divisor, {16{1'b0}}}), .out(multiplexer_1_out), .sel(rom_1_data[0]));
  Multiplexer #(.width(32), .enable("false")) multiplexer_2 (
    .in0(multiplexer_3_out), .in1({Dividend, {16{1'b0}}}), .out(multiplexer_2_out), .sel(rom_1_data[0]));
  Shifter #(.width(32), .shift("lr")) shifter_1 (.in(Divisor_q), .\dist (5'b00001), .out(shifter_1_out));
  Register #(.width(32)) u_Divisor (.D(multiplexer_1_out), .Q(Divisor_q), .clk(and_1_out));  // open: en, clr
  Multiplexer #(.width(16), .enable("false")) multiplexer_3 (
    .in0(Remainder), .in1(adder_1_out), .out(multiplexer_3_out[31:16]), .sel(Remainder[15]));
  Register #(.width(32)) u_Remainder (
    .D(multiplexer_2_out), .Q({Remainder_q, multiplexer_3_out[15:0]}), .clk(and_1_out));  // open: en, clr
  Subtractor #(.width(16)) subtractor_1 (.a(Remainder_q), .b(Divisor_q[31:16]), .out(Remainder));  // open: bin, bout
  Adder #(.width(16)) adder_1 (.a(Remainder), .b(Divisor_q[31:16]), .out(adder_1_out));  // open: cin, cout
  Multiplexer #(.width(16), .enable("false")) multiplexer_4 (
    .in0({Quotient[15:1], 1'b1}), .in1({Quotient[15:1], 1'b0}), .out(multiplexer_4_out), .sel(Remainder[15]));
  Register #(.width(16)) u_Quotient (
    .D(multiplexer_4_out), .Q(Quotient_q), .clk(and_1_out), .clr(rom_1_data[0]));  // open: en
  Shifter #(.width(16)) shifter_2 (.in(Quotient_q), .\dist (4'b0001), .out(Quotient));

  // Notes on the sheet:
  //   contents of rom_1 (hex, n*v repeats v):
  //   1
  //   Clock to Registers
  //   When the divisor and remainder are 0, this will keep shifting left and inserting a 1.
endmodule

module Negative_Tester (
  input  [15:0] Input,
  output [15:0] Absolute_Value,
  output Negated
);

  wire [15:0] negator_1_out;

  Negator #(.width(16)) negator_1 (.in(Input), .out(negator_1_out));
  Multiplexer #(.width(16), .enable("false")) multiplexer_1 (
    .in0(Input), .in1(negator_1_out), .out(Absolute_Value), .sel(Input[15]));

  assign Negated = Input[15];
endmodule
