// Logisim project Project 4 v1.circ as structural Verilog: 3 circuits, main circuit main
module main (
  input  [15:0] Operand_1__Multiplicand_or_Dividend,
  input  [15:0] Operand_2__Multiplier_and_Divisor,
  input  Mul,
  input  Div,
  output [31:0] Product,
  output M_Ready,
  output [15:0] Quotient,
  output [15:0] Remainder,
  output D_Ready
);

  wire Clock_out;

  Clock Clock (.out(Clock_out));
endmodule

module _16_bit_Multiplication (
  input  [15:0] Multiplicand,
  input  [15:0] Multiplier,
  input  Mul,
  input  Clock,
  output [31:0] Product,
  output M_Ready
);

  wire and_1_out, not_1_out, not_2_out;
  wire [7:0] counter_1_q, rom_1_data;
  wire [15:0] multiplexer_2_out, multiplier_q, undriven;
  wire [31:0] adder_1_out, multiplexer_1_out, multiplexer_3_out, multiplicand_q, product_q, shifter_1_out;

  Counter #(.ongoal("stay")) counter_1 (
    .Q(counter_1_q), .carry(M_Ready), .clk(and_1_out), .clr(not_1_out));  // open: load, D, count
  not not_1 (not_1_out, Mul);
  and and_1 (and_1_out, Mul, Clock);
  Multiplexer #(.width(32), .enable("false")) multiplexer_1 (
    .in0(shifter_1_out), .in1({{16{1'b0}}, Multiplicand}), .out(multiplexer_1_out), .sel(rom_1_data[0]));
  Multiplexer #(.width(16), .enable("false")) multiplexer_2 (
    .in0(undriven), .in1(Multiplier), .out(multiplexer_2_out), .sel(rom_1_data[0]));
  ROM rom_1 (.addr(counter_1_q), .data(rom_1_data));  // open: sel
  Register #(.width(32)) u_multiplicand (.D(multiplexer_1_out), .Q(multiplicand_q), .clk(and_1_out));  // open: en, clr
  Register #(.width(16)) u_multiplier (.D(multiplexer_2_out), .Q(multiplier_q), .clk(and_1_out));  // open: en, clr
  Shifter #(.width(32)) shifter_1 (.in(multiplicand_q), .\dist (5'b00001), .out(shifter_1_out));
  Multiplexer #(.width(32), .enable("false")) multiplexer_3 (
    .in0(multiplicand_q), .in1({32{1'b0}}), .out(multiplexer_3_out), .sel(not_2_out));
  not not_2 (not_2_out, multiplier_q[0]);
  Adder #(.width(32)) adder_1 (.a(product_q), .b(multiplexer_3_out), .out(adder_1_out));  // open: cin, cout
  Register #(.width(32)) u_product (.D(adder_1_out), .Q(product_q), .clk(and_1_out), .clr(rom_1_data[0]));  // open: en

  // Notes on the sheet:
  //   Multiplier/cand feedback?
  //   Clock to Registers
  //   When the Zero bit is 1, the product, multiplicand, and multiplier and initialized
endmodule

module _16_bit_Division (
  input  [15:0] Divisor,
  input  [15:0] Dividend,
  input  Div,
  input  Clock,
  output [15:0] Quotient,
  output [15:0] Remainder,
  output D_Ready
);

  wire and_1_out, not_1_out;
  wire [7:0] counter_1_q, rom_1_data;

  ROM rom_1 (.addr(counter_1_q), .data(rom_1_data));  // open: sel
  Counter #(.ongoal("stay")) counter_1 (
    .Q(counter_1_q), .carry(D_Ready), .clk(and_1_out), .clr(not_1_out));  // open: load, D, count
  not not_1 (not_1_out, Div);
  and and_1 (and_1_out, Div, Clock);

  // Notes on the sheet:
  //   Clock to Registers
endmodule
