// Logisim project left2plus5twice.circ as structural Verilog: 1 circuit, main circuit main
module main (
  input  [15:0] \input ,
  input  Mul,
  input  Clock,
  output [15:0] out_4,
  output out_5
);

  wire and_1_out, not_1_out;
  wire [7:0] counter_1_q, rom_1_data;
  wire [15:0] adder_1_out, multiplexer_1_out, multiplexer_2_out, shifter_1_out;

  Multiplexer #(.width(16)) multiplexer_1 (
    .in0(multiplexer_2_out), .in1(\input ), .out(multiplexer_1_out), .sel(rom_1_data[1]));  // open: en
  Counter #(.max('h6), .ongoal("stay"), .trigger("falling")) counter_1 (
    .Q(counter_1_q), .carry(out_5), .clk(and_1_out), .clr(not_1_out));  // open: load, D, count
  not not_1 (not_1_out, Mul);
  and and_1 (and_1_out, Mul, Clock);
  ROM rom_1 (.addr(counter_1_q), .data(rom_1_data));  // open: sel
  Register #(.width(16), .trigger("falling")) register_1 (
    .D(multiplexer_1_out), .en(rom_1_data[0]), .Q(out_4), .clk(and_1_out));  // open: clr
  Adder #(.width(16)) adder_1 (.a(16'h5), .b(out_4), .out(adder_1_out));  // open: cin, cout
  Shifter #(.width(16)) shifter_1 (.in(out_4), .\dist (4'b0010), .out(shifter_1_out));
  Multiplexer #(.width(16)) multiplexer_2 (
    .in0(adder_1_out), .in1(shifter_1_out), .out(multiplexer_2_out), .sel(rom_1_data[2]));  // open: en

  // Notes on the sheet:
  //   contents of rom_1 (hex, n*v repeats v):
  //   0 3 5 1 5 1
  //   Clock to Registers
endmodule
