// Logisim project Brendan_Drusda_Lab10.circ as structural Verilog: 4 circuits, main circuit main
module main (
);

  wire clock_1_out, control_unit_1_dstmux, fields_1_register, not_1_out;
  wire [1:0] control_unit_1_alu;
  wire [3:0] fields_1_op_code;
  wire [7:0] A_q, adder_1_out, alu_1_output, B_q, fields_1_immediate, multiplexer_1_out, PC_q;
  wire [15:0] rom_1_data;

  Register #(.trigger("falling")) PC (.D(adder_1_out), .en(1'b1), .Q(PC_q), .clk(clock_1_out));  // open: clr
  Clock clock_1 (.out(clock_1_out));
  Adder adder_1 (.a(PC_q), .b(8'h1), .out(adder_1_out));  // open: cin, cout
  ROM #(.dataWidth(16)) rom_1 (.addr(PC_q), .data(rom_1_data), .sel(1'b1));
  Fields fields_1 (
    .Instruction(rom_1_data), .Op_Code(fields_1_op_code), .Register(fields_1_register),
    .Immediate(fields_1_immediate));
  Control_Unit control_unit_1 (.Op_Code(fields_1_op_code), .ALU(control_unit_1_alu), .DstMux(control_unit_1_dstmux));
  not not_1 (not_1_out, fields_1_register);
  Register A (.D(multiplexer_1_out), .en(not_1_out), .Q(A_q), .clk(clock_1_out));  // open: clr
  Register B (.D(multiplexer_1_out), .en(fields_1_register), .Q(B_q), .clk(clock_1_out));  // open: clr
  ALU alu_1 (.A(A_q), .B(B_q), .Op(control_unit_1_alu), .Output(alu_1_output));
  Multiplexer #(.width(8), .enable("false")) multiplexer_1 (
    .in0(alu_1_output), .in1(fields_1_immediate), .out(multiplexer_1_out), .sel(control_unit_1_dstmux));

  // Notes on the sheet:
  //   contents of rom_1 (hex, n*v repeats v):
  //   1 802 2005 3801 0 801 4000 5000 0 5800
  //   SetMux
endmodule

module ALU (
  input  [1:0] Op,
  input  [7:0] A,
  input  [7:0] B,
  output [7:0] Output
);

  wire [7:0] adder_1_out, and_1_out, or_1_out, subtractor_1_out;

  assign and_1_out = A & B;  // AND_Gate and_1, 8 bits wide
  assign or_1_out = A | B;  // OR_Gate or_1, 8 bits wide
  Adder adder_1 (.a(A), .b(B), .out(adder_1_out));  // open: cin, cout
  Subtractor subtractor_1 (.a(A), .b(B), .out(subtractor_1_out));  // open: bin, bout
  Multiplexer #(.select(2), .width(8), .enable("false")) multiplexer_1 (
    .in0(adder_1_out), .in1(subtractor_1_out), .in2(or_1_out), .in3(and_1_out), .out(Output), .sel(Op));
endmodule

module Fields (
  input  [15:0] Instruction,
  output [3:0] Op_Code,
  output Register,
  output [7:0] Immediate
);


  assign Immediate = Instruction[7:0];
  assign Op_Code = Instruction[15:12];
  assign Register = Instruction[11];
endmodule

// Decoder
module Control_Unit (
  input  [3:0] Op_Code,
  output [1:0] ALU,
  output DstMux
);

  wire not_2_out, not_3_out;

  not not_1 (ALU[1], Op_Code[1]);
  not not_2 (not_2_out, Op_Code[1]);
  not not_3 (not_3_out, Op_Code[2]);
  and and_1 (DstMux, not_2_out, not_3_out);

  assign ALU[0] = Op_Code[0];
endmodule
