// Logisim project Lab8_B.circ as structural Verilog: 4 circuits, main circuit main
module main (
);

  wire and_1_out, clock_1_out, kmap_1_out_5;
  wire [1:0] n1_1_n0, register_1_q;
  wire [3:0] counter_1_q;

  Clock clock_1 (.out(clock_1_out));
  Counter #(.width(4), .max('hf)) counter_1 (.Q(counter_1_q), .clk(clock_1_out));  // open: load, D, count, carry, clr
  // Probe on kmap_1_out_5
  kmap kmap_1 (.A(counter_1_q[3]), .B(counter_1_q[2]), .C(counter_1_q[1]), .D(counter_1_q[0]), .out_5(kmap_1_out_5));
  Register #(.width(2)) register_1 (.D(n1_1_n0), .Q(register_1_q), .clk(clock_1_out));  // open: en, clr
  and and_1 (and_1_out, register_1_q[1], register_1_q[0]);
  LED led_1 (.in(and_1_out));
  N1 n1_1 (.Input(kmap_1_out_5), .S1(register_1_q[1]), .S0(register_1_q[0]), .N0(n1_1_n0[0]));
  N0 n0_1 (.Input(kmap_1_out_5), .S1(register_1_q[1]), .S0(register_1_q[0]), .N0(n1_1_n0[1]));
  // Probe on n1_1_n0
endmodule

module kmap (
  input  A,
  input  B,
  input  C,
  input  D,
  output out_5
);

  wire and_1_out, and_2_out, and_3_out;

  and and_1 (and_1_out, ~D, B);  // AND_Gate
  and and_2 (and_2_out, D, ~C);  // AND_Gate
  and and_3 (and_3_out, ~C, ~A);  // AND_Gate
  or or_1 (out_5, and_3_out, and_1_out, and_2_out);
endmodule

module N0 (
  input  Input,
  input  S1,
  input  S0,
  output N0
);

  wire and_1_out, and_2_out;

  and and_1 (and_1_out, Input, S0);
  and and_2 (and_2_out, Input, S1);
  or or_1 (N0, and_1_out, and_2_out);
endmodule

module N1 (
  input  Input,
  input  S1,
  input  S0,
  output N0
);

  wire and_1_out, and_2_out;

  and and_1 (and_1_out, Input, ~S0);  // AND_Gate
  and and_2 (and_2_out, Input, S1);
  or or_1 (N0, and_1_out, and_2_out);
endmodule
