// Logisim project Brendan_Drusda_Lab9.circ as structural Verilog: 1 circuit, main circuit main
module main (
  input  Write_Enable,
  input  [2:0] Read_Register_1,
  input  [2:0] Read_Register_2,
  input  [2:0] Write_Register,
  input  [31:0] Write_Data,
  output [31:0] Read_Data_1,
  output [31:0] Read_Data_2
);

  wire clock_1_out;
  wire [31:0] Register_0_q, Register_1_q, Register_2_q, Register_3_q, Register_4_q, Register_5_q,
       Register_6_q, Register_7_q;

  Decoder #(.select(3), .enable("false")) decoder_1 (.sel(Read_Register_1));  // open: out0, out1, out2, out3, out4, out5, out6, out7
  Decoder #(.select(3), .enable("false")) decoder_2 (.sel(Read_Register_2));  // open: out0, out1, out2, out3, out4, out5, out6, out7
  Decoder #(.select(3), .enable("false")) decoder_3 (.sel(Write_Register));  // open: out0, out1, out2, out3, out4, out5, out6, out7
  Clock clock_1 (.out(clock_1_out));
  Register #(.width(32)) Register_0 (.Q(Register_0_q), .clk(clock_1_out));  // open: D, en, clr
  Register #(.width(32)) Register_1 (.Q(Register_1_q), .clk(clock_1_out));  // open: D, en, clr
  Register #(.width(32)) Register_2 (.Q(Register_2_q), .clk(clock_1_out));  // open: D, en, clr
  Register #(.width(32)) Register_3 (.Q(Register_3_q), .clk(clock_1_out));  // open: D, en, clr
  Register #(.width(32)) Register_4 (.Q(Register_4_q), .clk(clock_1_out));  // open: D, en, clr
  Register #(.width(32)) Register_5 (.Q(Register_5_q), .clk(clock_1_out));  // open: D, en, clr
  Register #(.width(32)) Register_6 (.Q(Register_6_q), .clk(clock_1_out));  // open: D, en, clr
  Register #(.width(32)) Register_7 (.Q(Register_7_q), .clk(clock_1_out));  // open: D, en, clr
  Multiplexer #(.select(3), .width(32)) multiplexer_1 (
    .in0(Register_0_q), .in1(Register_1_q), .in2(Register_2_q), .in3(Register_3_q), .in4(Register_4_q),
    .in5(Register_5_q), .in6(Register_6_q), .in7(Register_7_q));  // open: out, sel, en
endmodule
